# Fritzing sketch Irrigation Components Wiring (saved by Fritzing 0.9.3b)

parts:
  Raspberry_Pi_4 = Raspberry Pi 3 [part_number=RPI-3-V1.2]
  Part3 = FC-28 Soil Hygrometer Module
  Part4 = Soil Moisture Sensor
  hc-sr4 = hc-sr04
  R8 = Resistor [tolerance=±5% resistance=2.2k package="2010 [SMD]"]
  R9 = Resistor [tolerance=±5% resistance=1k package="2010 [SMD]"]

nets:
  3V3: Raspberry_Pi_4.3v3, Part3.VCC
  N1: Raspberry_Pi_4.GPIO16, Part3.DO
  N2: Raspberry_Pi_4.GPIO24, R8.Pin_1, R9.Pin_1
  N3: Raspberry_Pi_4.GPIO23, hc-sr4.Trig
  GND: Raspberry_Pi_4.GND, hc-sr4.GND
  N4: Part3.POS, Part4.VCC
  N5: Part3.NEG, Part4.GND
  N6: hc-sr4.Echo, R9.Pin_0

custom parts:
  FC-28 Soil Hygrometer Module: The FC-28 is a soil hygrometer module that uses the Texas Instruments LM393 comparator chip to provide an analog measurement of soil humidity. The digital output is high when soil moisture is over a certain threshold, as determined by adjusting the potentiometer.
