# Fritzing sketch Token Input Components Wiring (saved by Fritzing 0.9.3b)

parts:
  Raspberry_Pi_2 = Raspberry Pi 3 [part_number=RPI-3-V1.2]
  S8 = Pushbutton [package="[SMD]"]
  S9 = Pushbutton [package="[SMD]"]
  S10 = Pushbutton [package="[SMD]"]
  S11 = Pushbutton [package="[SMD]"]
  S12 = Pushbutton [package="[SMD]"]
  S13 = Pushbutton [package="[SMD]"]
  Grove2 = Grove OLED 128x96

nets:
  3V3: Raspberry_Pi_2.3v3, Grove2.VCC
  N1: Raspberry_Pi_2.GPIO2, Grove2.SDA
  N2: Raspberry_Pi_2.GPIO3, Grove2.SCL
  GND: Raspberry_Pi_2.GND, Grove2.GND
  N3: Raspberry_Pi_2.GPIO17, S10.Pin_1
  N4: Raspberry_Pi_2.GPIO27, S12.Pin_1
  N5: Raspberry_Pi_2.GPIO22, S13.Pin_1
  N6: Raspberry_Pi_2.GPIO10, S11.Pin_1
  N7: Raspberry_Pi_2.GPIO9, S9.Pin_1, S9.Pin_2
  N8: Raspberry_Pi_2.GPIO11, S8.Pin_1, S8.Pin_2
